# Fritzing sketch lm386 (saved by Fritzing 1.0.2b)
circuit board: 8.46667cm x 5.64444cm
stripboards: 1

parts:
  LM386 = LM386 [package=dip08]
  R1 = Resistor [tolerance=±5% resistance=1k package="0805 [SMD]"]
  R2 = Resistor [tolerance=±5% resistance=10k package="0805 [SMD]"]
  C1_100uf = Capacitor Polarized [package=cpol-radial-100uf-25v]
  C3_100uf = Capacitor Polarized [package=cpol-radial-100uf-25v]
  C2_100uf = Capacitor Polarized [package=cpol-radial-100uf-25v]
  C7 = Film/Foil Capacitor [capacitance=100nF voltage=35V package="5mm [THT, pp]"]
  R3 = TRIMPOT [maximum_resistance=10kΩ knob_status=50% power=0.5W package=3386u]
  R5 = Resistor [tolerance=±5% power=0.25W resistance=100 package=THT]
  C6 = Electrolytic Capacitor [capacitance=1µF voltage=35V package="0807 [SMD, electrolytic]"]
  J2 = Screw terminal - 2 pins [package=THT]
  J1 = Dagu DGServo 9g header connector (female) [package=THT]

nets:
  GND: LM386.-IN, LM386.V-, R1.Pin_0, C1_100uf.-, R3.CW, R5.Pin_1, C6.-, J2.pin1
  N1: LM386.+IN, R1.Pin_1, R2.Pin_1
  N2: LM386.OUT, C2_100uf.+, C7.-
  5V: LM386.V+, C1_100uf.+
  N3: LM386.BP, C6.+
  N4: R2.Pin_0, R3.WIPER
  3.3v Audio IN: C3_100uf.+, J1.Vcc
  N5: C3_100uf.-, R3.CCW
  N6: C2_100uf.-, J2.pin2
  N7: C7.+, R5.Pin_0
