# Fritzing sketch sean (saved by Fritzing 1.0.2b)
perfboards: 1

parts:
  C1 = Capacitor Polarized [package=cpol-radial-10uf-25v]  # not connected
  J1 = female pin header, 15 pins [form="♀ (female)"]  # not connected
  J2 = female pin header, 15 pins [form="♀ (female)"]  # not connected
  U1 = LuaNode32 / ESP32 [part_number=ESP32S-PIN30]  # not connected
  J3 = female pin header, 10 pins [form="♀ (female)"]  # not connected
  A1 = lcd color display 1.3in 240x240 7pin interface [package=THT]
  R1 = Resistor [tolerance=±5% resistance=10k package="0402 [SMD]"]
  R2 = Resistor [tolerance=±5% resistance=22k package="2512 [SMD]"]
  R3 = Resistor [tolerance=±5% resistance=22k package="2512 [SMD]"]
  Part1 = Adafruit ADS1115 16Bit I2C ADC [part_number="Adafruit #1085"]  # not connected
  LED1 = smd LED [color="Red (633nm)" package="0805 [SMD]"]
  R4 = Resistor [tolerance=±5% resistance=470 package="0805 [SMD]"]
  Speaker = Header 3 [package=screwterminal-3.5mm-3_lock.007s]
  R5 = Resistor [tolerance=±5% power=0.25W resistance=4.7k package=THT]
  DS18B20 = Header 3 [package=screwterminal-3.5mm-3_lock.007s]
  S1 = Pushbutton [package=THT]  # not connected
  S2 = Pushbutton [package=THT]  # not connected
  A0 = female pin header, 2 pins [form="♀ (female)"]
  A1_2 = female pin header, 2 pins [form="♀ (female)"]
  X1 = USB Connectors [package=usb-a-s-nosilk-female]
  S3 = Toggle Switch [package=THT]
  R6 = Resistor [tolerance=±5% resistance=100k package="2512 [SMD]"]  # not connected
  R7 = Resistor [tolerance=±5% resistance=100k package="2512 [SMD]"]
  Q1 = NPN-Transistor [package="TO92 [THT]"]
  R8 = Resistor [tolerance=±5% resistance=1k package="2512 [SMD]"]  # not connected

nets:
  N1: A1.VCC, R5.Pin_1
  N2: A1.BLK, R1.Pin_1
  N3: R2.Pin_0, R3.Pin_0, DS18B20.3
  N4: R2.Pin_1, A0.pin2
  N5: R3.Pin_1, A1_2.pin2
  N6: LED1.anode, R4.Pin_1
  N7: Speaker.1, S3.L1
  N8: Speaker.2, Q1.B
  N9: Speaker.3, X1.VBUS
  N10: R5.Pin_0, DS18B20.1
  N11: DS18B20.2, R7.Pin_0
  N12: X1.GND, S3.COM

custom parts:
  LuaNode32 / ESP32: New Image for LuaNode32 DOIT ESP32 DEVKIT V1. Base parts from LuaNode32 / ESP32 ESP32 based LuaNode32 by G.Noorlander DOIT Esp32 DevKit v1 (30 pins long, 11 pins width) by Werner Rothschopf (modified by vanepp Dec 2018)
  lcd color display 1.3in 240x240 7pin interface: 1.3 Inch Color 240 x 240 IPS TFT LCD Display Screen Module Board 7 Pin 4 Wire ST7789VW Drive IC SPI interface.
  Adafruit ADS1115 16Bit I2C ADC: For microcontrollers without an analog-to-digital converter or when you want a higher-precision ADC, the ADS1115 provides 16-bit precision at 860 samples/second over I2C. The chip can be configured as 4 single-ended input channels, or two differential channels. As a nice bonus, it even includes a programmable gain amplifier, up to x16, to help boost up smaller single/differential signals to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
